# Fritzing sketch collegamentiAutoDistanza (saved by Fritzing 0.9.2b)
breadboards: 1

parts:
  Componente3 = Arduino Uno (Rev3)
  IC3 = L293D [package=THT]
  M3 = DC Motor
  M4 = DC Motor
  VCC2 = 4 x AAA Battery Mount
  Componente4 = SRF05 Ultrasonic Rangefinder  # not connected

nets:
  N1: Componente3.D10_PWM/SS, IC3.In_4
  N2: Componente3.D11_PWM/MOSI, IC3.In_3
  N3: Componente3.D3_PWM, IC3.In_1
  N4: Componente3.D4, IC3.In_2
  N5: Componente3.D6_PWM, IC3.Enable_2
  N6: Componente3.D7, IC3.Enable_1
  N7: Componente3.GND, IC3.0V, IC3.+Vmotor, VCC2.-, VCC2.+
  N8: IC3.Out_1_(_Controlled_by_Enable_1_), M4.pin_2
  N9: IC3.Out_2_(_Controlled_by_Enable_1_), M4.pin_1
  N10: IC3.Out_3_(_Controlled_by_Enable_2_), M3.pin_2
  N11: IC3.Out_4_(_Controlled_by_Enable_2_), M3.pin_1
